// Logisim project simplified_circuit.circ as structural Verilog: 1 circuit, main circuit main
module main (
  input  RESET,
  input  bit_in,
  output bit_out
);

  wire bitselector_1_out, demultiplexer_1_out0, demultiplexer_1_out1, demultiplexer_1_out2,
       demultiplexer_1_out3, input_reg_q, multiplexer_1_out, multiplexer_2_out, multiplexer_3_out,
       multiplexer_4_out;
  wire [1:0] adder_1_out, counter_1_q, DFF_en_2_q, DFF_en_4_q, multiplier_1_out, undriven, undriven_2;

  Clock clock_1 (.out(RESET));
  D_Flip_Flop input_reg (.clk(RESET), .D(bit_in), .Q(input_reg_q), .preset(RESET));  // open: Qn, en, reset
  Multiplexer #(.enable("false")) multiplexer_1 (
    .in0(DFF_en_2_q[1]), .in1(input_reg_q), .out(multiplexer_1_out), .sel(demultiplexer_1_out3));
  Multiplexer #(.enable("false")) multiplexer_2 (
    .in0(DFF_en_4_q[0]), .in1(input_reg_q), .out(multiplexer_2_out), .sel(demultiplexer_1_out0));
  Multiplexer #(.enable("false")) multiplexer_3 (
    .in0(DFF_en_4_q[1]), .in1(input_reg_q), .out(multiplexer_3_out), .sel(demultiplexer_1_out1));
  Multiplexer #(.enable("false")) multiplexer_4 (
    .in0(DFF_en_2_q[0]), .in1(input_reg_q), .out(multiplexer_4_out), .sel(demultiplexer_1_out2));
  Demultiplexer #(.select(2), .enable("false")) demultiplexer_1 (
    .out0(demultiplexer_1_out0), .out1(demultiplexer_1_out1), .out2(demultiplexer_1_out2),
    .out3(demultiplexer_1_out3), .in(1'b1), .sel(adder_1_out));
  D_Flip_Flop DFF_en (.clk(RESET), .D(multiplexer_3_out), .Q(DFF_en_4_q[1]), .preset(RESET));  // open: Qn, en, reset
  D_Flip_Flop DFF_en_2 (.clk(RESET), .D(multiplexer_4_out), .Q(DFF_en_2_q[0]), .preset(RESET));  // open: Qn, en, reset
  D_Flip_Flop DFF_en_3 (.clk(RESET), .D(multiplexer_1_out), .Q(DFF_en_2_q[1]), .preset(RESET));  // open: Qn, en, reset
  Counter #(.width(2), .max('h3)) counter_1 (
    .count(1'b1), .Q(counter_1_q), .clk(RESET), .clr(RESET));  // open: load, D, carry
  D_Flip_Flop DFF_en_4 (.clk(RESET), .D(multiplexer_2_out), .Q(DFF_en_4_q[0]), .preset(RESET));  // open: Qn, en, reset
  Multiplier #(.width(2)) multiplier_1 (.a(counter_1_q), .b(undriven), .out(multiplier_1_out));  // open: cin, cout
  BitSelector #(.width(4)) bitselector_1 (.in({DFF_en_2_q, DFF_en_4_q}), .out(bitselector_1_out), .sel(adder_1_out));
  Adder #(.width(2)) adder_1 (.a(multiplier_1_out), .b(undriven_2), .out(adder_1_out));  // open: cin, cout
  D_Flip_Flop output_reg (.clk(RESET), .D(bitselector_1_out), .Q(bit_out), .preset(RESET));  // open: Qn, en, reset

  // Notes on the sheet:
  //   bit_in: pull=up
  //   CLOCK
  //   bit_in_inside
  //   enables
  //   count
  //   counter
  //   3
  //   memory_in_the_middle
  //   45
  //   a
  //   bit_out_inside
  //   bit_out
endmodule
